# Fritzing sketch Diagram (saved by Fritzing 0.9.3b)
circuit board: 8.46667cm x 5.64444cm
breadboards: 1

parts:
  Pro_Micro1 = SparkFun Pro Micro
  Part1 = MicroSD Card Module
  Red_LED = smd LED [color="Red (633nm)" package="1206 [SMD]"]
  Green_LED = smd LED [color="Red (633nm)" package="1206 [SMD]"]
  R1 = Resistor [tolerance=±5% resistance=220 package="0603 [SMD]"]

nets:
  GND: Pro_Micro1.GND, Part1.GND, R1.Pin_0
  N1: Pro_Micro1.2, Red_LED.anode
  N2: Pro_Micro1.3, Pro_Micro1.4, Green_LED.anode
  N3: Pro_Micro1.10, Part1.CS
  N4: Pro_Micro1.16, Part1.MOSI
  N5: Pro_Micro1.14, Part1.MISO
  N6: Pro_Micro1.15, Part1.SCK
  VCC: Pro_Micro1.VCC, Part1.VCC
  N7: Red_LED.cathode, Green_LED.cathode, R1.Pin_1

custom parts:
  SparkFun Pro Micro: The Pro Micro is similar to the Pro Mini except with an ATmega32U4 on board. The USB transceiver inside the 32U4 allows us to add USB connectivity on-board and do away with bulky external USB interface. Based on: https://github.com/unorthodox-engineers/unorthodox-arduino/blob/master/Unorthodox/fritzing/parts/Pro%20Micro.fzpz
